# Fritzing sketch Sketch (saved by Fritzing 0.8.5b)
circuit board: 9.15342cm x 7.17783cm
breadboards: 1

parts:
  Raspberry_Pi_B_rev1 = Raspberry Pi B rev2
  IC1 = L293D [package=THT]
  IC2 = L293D [package=THT]
  IC3 = L293D [package=THT]
  M1 = Stepper Motor - Bipolar
  M3 = DC Motor
  M2 = Stepper Motor - Bipolar

nets:
  N1: Raspberry_Pi_B_rev1.5V, IC1.Enable_1, IC1.+Vmotor, IC1.Enable_2, IC1.+V, IC2.Enable_1, IC2.+Vmotor, IC2.Enable_2, IC2.+V, IC3.Enable_1, IC3.+Vmotor, IC3.Enable_2, IC3.+V
  N2: Raspberry_Pi_B_rev1.GND, IC1.0V, IC2.0V, IC3.0V
  N3: Raspberry_Pi_B_rev1.GPIO_23, IC1.In_1
  N4: Raspberry_Pi_B_rev1.GPIO_14, IC2.In_2
  N5: Raspberry_Pi_B_rev1.GPIO_17, IC1.In_3
  N6: Raspberry_Pi_B_rev1.GPIO_18, IC1.In_4
  N7: Raspberry_Pi_B_rev1.GPIO_22, IC1.In_2
  N8: Raspberry_Pi_B_rev1.GPIO_4, IC2.In_1
  N9: Raspberry_Pi_B_rev1.GPIO_10, IC3.In_2
  N10: Raspberry_Pi_B_rev1.GPIO_9, IC3.In_1
  N11: Raspberry_Pi_B_rev1.GPIO_8, IC3.In_3
  N12: Raspberry_Pi_B_rev1.GPIO_7, IC3.In_4
  N13: IC1.Out_1_(_Controlled_by_Enable_1_), M2.D
  N14: IC1.Out_2_(_Controlled_by_Enable_1_), M2.B
  N15: IC1.Out_3_(_Controlled_by_Enable_2_), M2.A
  N16: IC1.Out_4_(_Controlled_by_Enable_2_), M2.C
  N17: IC2.Out_1_(_Controlled_by_Enable_1_), M3.pin_2
  N18: IC2.Out_2_(_Controlled_by_Enable_1_), M3.pin_1
  N19: IC3.Out_1_(_Controlled_by_Enable_1_), M1.C
  N20: IC3.Out_2_(_Controlled_by_Enable_1_), M1.A
  N21: IC3.Out_3_(_Controlled_by_Enable_2_), M1.B
  N22: IC3.Out_4_(_Controlled_by_Enable_2_), M1.D
